# Fritzing sketch schematic (saved by Fritzing 0.9.3b)
breadboards: 1

parts:
  Motortreiber = EasyDriver_v44
  12V_DC = Power plug
  Mikrocontroller = ESP8266 NodeMCU LoLin module
  Mikroschalter = JL012-13-5.2 Lever (Limit) Switch SPDT + NO + NC [part_number=JL012-13-5.2]
  Schrittmotor = Stepper Motor - Bipolar

nets:
  GND: Motortreiber.GND, 12V_DC.GND, Mikrocontroller.GND, Mikroschalter.C
  N1: Motortreiber.V+, 12V_DC.VCC
  N2: Motortreiber.STEP, Mikrocontroller.D2
  N3: Motortreiber.DIR, Mikrocontroller.D1
  N4: Motortreiber.OUT2A, Schrittmotor.D
  N5: Motortreiber.OUT2B, Schrittmotor.B
  N6: Motortreiber.OUT1A, Schrittmotor.A
  N7: Motortreiber.OUT1B, Schrittmotor.C
  N8: Mikrocontroller.D5, Mikroschalter.NO

custom parts:
  ESP8266 NodeMCU LoLin module: ESP8266 based NodeMCU
  JL012-13-5.2 Lever (Limit) Switch SPDT + NO + NC: Micro Switch; Model No.: JL012-13.5-2; Actuator Action: Momentary; Actuator Type: Hinge Lever; Contact Configuration: 1NO, 1NC (SPDT) Temperature -25~65℃；Relative humidity: below 85%; Rate Voltage: 125V AC; Rated Current: 1A.
